// Digital circuit 16to1from8to1multiplexer.dig as structural Verilog
module _16to1from8to1multiplexer (
  input  I_0,
  input  I_1,
  input  I_2,
  input  I_3,
  input  I_4,
  input  I_5,
  input  I_6,
  input  I_7,
  input  I_8,
  input  I_9,
  input  I_10,
  input  I_11,
  input  I_12,
  input  I_13,
  input  I_14,
  input  I_15,
  input  S_0,
  input  S_1,
  input  S_2,
  input  S_3,
  output O
);

  wire _8to1multiplexer_1_o, _8to1multiplexer_2_o, not_1_out;

  not not_1 (not_1_out, S_3);
  _8to1multiplexer _8to1multiplexer_1 (
    .S_0(S_0), .S_1(S_1), .S_2(S_2), .E(not_1_out), .I_0(I_0), .I_1(I_1), .I_2(I_2), .I_3(I_3), .I_4(I_4),
    .I_5(I_5), .I_6(I_6), .I_7(I_7), .O(_8to1multiplexer_1_o));
  _8to1multiplexer _8to1multiplexer_2 (
    .S_0(S_0), .S_1(S_1), .S_2(S_2), .E(S_3), .I_0(I_8), .I_1(I_9), .I_2(I_10), .I_3(I_11), .I_4(I_12),
    .I_5(I_13), .I_6(I_14), .I_7(I_15), .O(_8to1multiplexer_2_o));
  or or_1 (O, _8to1multiplexer_1_o, _8to1multiplexer_2_o);
endmodule
