// Digital circuit 16to4from8to3encoder.dig as structural Verilog
module _16to4from8to3encoder (
  input  I_0,
  input  I_1,
  input  I_2,
  input  I_3,
  input  I_4,
  input  I_5,
  input  I_6,
  input  I_7,
  input  I_8,
  input  I_9,
  input  I_10,
  input  I_11,
  input  I_12,
  input  I_13,
  input  I_14,
  input  I_15,
  output O_2,
  output O_1,
  output O_0,
  output V,
  output O_3
);

  wire _8to3encoder_1_o_0, _8to3encoder_1_o_1, _8to3encoder_1_o_2, _8to3encoder_1_v, _8to3encoder_2_o_0,
       _8to3encoder_2_o_1, _8to3encoder_2_o_2;

  _8to3encoder _8to3encoder_1 (
    .I_0(I_0), .I_2(I_1), .I_3(I_2), .I_4(I_3), .I_5(I_4), .I_6(I_5), .I_7(I_6), .I_1(I_7),
    .O_2(_8to3encoder_1_o_2), .O_1(_8to3encoder_1_o_1), .O_0(_8to3encoder_1_o_0), .V(_8to3encoder_1_v));
  _8to3encoder _8to3encoder_2 (
    .I_0(I_8), .I_2(I_9), .I_3(I_10), .I_4(I_11), .I_5(I_12), .I_6(I_13), .I_7(I_14), .I_1(I_15),
    .O_2(_8to3encoder_2_o_2), .O_1(_8to3encoder_2_o_1), .O_0(_8to3encoder_2_o_0), .V(O_3));
  or or_1 (O_2, _8to3encoder_1_o_2, _8to3encoder_2_o_2);
  or or_2 (O_1, _8to3encoder_1_o_1, _8to3encoder_2_o_1);
  or or_3 (O_0, _8to3encoder_1_o_0, _8to3encoder_2_o_0);
  or or_4 (V, _8to3encoder_1_v, O_3);
endmodule
