// Digital circuit 1scounter.dig as structural Verilog
module _1scounter (
  input  C,
  input  I,
  output O
);

  wire and_1_out, and_2_out, and_3_out, and_4_out, not_1_out, not_2_out, not_3_out, or_1_out, or_2_out,
       Z_0_n_q, Z_1_n_q;

  not not_1 (not_1_out, I);
  not not_2 (not_2_out, Z_1_n_q);
  not not_3 (not_3_out, Z_0_n_q);
  and and_1 (and_1_out, I, Z_0_n_q);
  and and_2 (and_2_out, not_1_out, Z_1_n_q);
  and and_3 (and_3_out, I, not_3_out, not_2_out);
  and and_4 (and_4_out, not_1_out, Z_0_n_q);
  and and_5 (O, I, Z_1_n_q);
  or or_1 (or_1_out, and_1_out, and_2_out);
  or or_2 (or_2_out, and_3_out, and_4_out);
  D_FF Z_1_n (.D(or_1_out), .C(C), .Q(Z_1_n_q));  // open: nQ
  D_FF Z_0_n (.D(or_2_out), .C(C), .Q(Z_0_n_q));  // open: nQ
endmodule
