// Digital circuit 1to8demultiplexer.dig as structural Verilog
module _1to8demultiplexer (
  input  I,
  input  E,
  input  S2,
  input  S1,
  input  S0,
  output O0,
  output O1,
  output O2,
  output O3,
  output O4,
  output O5,
  output O6,
  output O7
);

  wire _3to8decoder_1_o0, _3to8decoder_1_o1, _3to8decoder_1_o2, _3to8decoder_1_o3, _3to8decoder_1_o4,
       _3to8decoder_1_o5, _3to8decoder_1_o6, _3to8decoder_1_o7;

  _3to8decoder _3to8decoder_1 (
    .E(E), .I2(S2), .I1(S1), .I0(S0), .O0(_3to8decoder_1_o0), .O1(_3to8decoder_1_o1), .O2(_3to8decoder_1_o2),
    .O3(_3to8decoder_1_o3), .O4(_3to8decoder_1_o4), .O5(_3to8decoder_1_o5), .O6(_3to8decoder_1_o6),
    .O7(_3to8decoder_1_o7));
  and and_1 (O0, _3to8decoder_1_o0, I);
  and and_2 (O1, _3to8decoder_1_o1, I);
  and and_3 (O2, _3to8decoder_1_o2, I);
  and and_4 (O3, _3to8decoder_1_o3, I);
  and and_5 (O4, _3to8decoder_1_o4, I);
  and and_6 (O5, _3to8decoder_1_o5, I);
  and and_7 (O6, _3to8decoder_1_o6, I);
  and and_8 (O7, _3to8decoder_1_o7, I);
endmodule
