// Digital circuit 1to8demultiplexerfrom3to8decoder.dig as structural Verilog
module _1to8demultiplexerfrom3to8decoder (
  input  I,
  input  S_0,
  input  S_1,
  input  S_2,
  input  E,
  output O_0,
  output O_1,
  output O_2,
  output O_3,
  output O_4,
  output O_5,
  output O_6,
  output O_7
);

  wire _3to8decoder_1_o0, _3to8decoder_1_o1, _3to8decoder_1_o2, _3to8decoder_1_o3, _3to8decoder_1_o4,
       _3to8decoder_1_o5, _3to8decoder_1_o6, _3to8decoder_1_o7;

  _3to8decoder _3to8decoder_1 (
    .E(E), .I2(S_2), .I1(S_1), .I0(S_0), .O0(_3to8decoder_1_o0), .O1(_3to8decoder_1_o1),
    .O2(_3to8decoder_1_o2), .O3(_3to8decoder_1_o3), .O4(_3to8decoder_1_o4), .O5(_3to8decoder_1_o5),
    .O6(_3to8decoder_1_o6), .O7(_3to8decoder_1_o7));
  and and_1 (O_0, I, _3to8decoder_1_o0);
  and and_2 (O_1, I, _3to8decoder_1_o1);
  and and_3 (O_2, I, _3to8decoder_1_o2);
  and and_4 (O_3, I, _3to8decoder_1_o3);
  and and_5 (O_4, I, _3to8decoder_1_o4);
  and and_6 (O_5, I, _3to8decoder_1_o5);
  and and_7 (O_6, I, _3to8decoder_1_o6);
  and and_8 (O_7, I, _3to8decoder_1_o7);
endmodule
