// Digital circuit 2to4decoder.dig as structural Verilog
module _2to4decoder (
  input  E,
  input  I_0,
  input  I_1,
  output O_0,
  output O_1,
  output O_2,
  output O_3
);

  wire not_1_out, not_2_out;

  not not_1 (not_1_out, I_0);
  not not_2 (not_2_out, I_1);
  and and_1 (O_0, E, not_1_out, not_2_out);
  and and_2 (O_1, E, I_0, not_2_out);
  and and_3 (O_2, E, not_1_out, I_1);
  and and_4 (O_3, E, I_0, I_1);
endmodule
