// Digital circuit 3dot10function.dig as structural Verilog
module _3dot10function (
  input  a,
  input  b,
  input  c,
  output q
);

  wire and_1_out, and_2_out, and_3_out, not_1_out, not_2_out, not_3_out;

  not not_1 (not_1_out, a);
  not not_2 (not_2_out, c);
  not not_3 (not_3_out, b);
  and and_1 (and_1_out, not_1_out, b, not_2_out);
  and and_2 (and_2_out, a, b, c);
  and and_3 (and_3_out, a, not_3_out, c);
  or or_1 (q, and_1_out, and_2_out, and_3_out);
endmodule
