// Digital circuit 3dot11function.dig as structural Verilog
module _3dot11function (
  input  a,
  input  b,
  input  c,
  output q
);

  wire and_1_out, and_2_out, and_3_out, and_4_out, and_5_out, and_6_out, not_1_out, not_2_out, not_3_out,
       or_1_out, or_2_out;

  not not_1 (not_1_out, a);
  not not_2 (not_2_out, c);
  not not_3 (not_3_out, b);
  and and_1 (and_1_out, not_1_out, not_3_out, not_2_out);
  and and_2 (and_2_out, not_1_out, b, not_2_out);
  and and_3 (and_3_out, not_1_out, b, c);
  and and_4 (and_4_out, a, not_3_out, not_2_out);
  and and_5 (and_5_out, a, not_3_out, c);
  and and_6 (and_6_out, a, b, not_2_out);
  or or_1 (or_1_out, and_1_out, and_2_out, and_3_out);
  or or_2 (or_2_out, and_4_out, and_5_out, and_6_out);
  or or_3 (q, or_1_out, or_2_out);
endmodule
