// Digital circuit 3dot12function.dig as structural Verilog
module _3dot12function (
  input  a,
  input  b,
  input  c,
  output q
);

  wire not_1_out, not_2_out, not_3_out, or_1_out, or_2_out;

  not not_1 (not_1_out, a);
  not not_2 (not_2_out, c);
  not not_3 (not_3_out, b);
  or or_1 (or_1_out, not_1_out, not_3_out, not_2_out);
  or or_2 (or_2_out, a, b, not_2_out);
  and and_1 (q, or_1_out, or_2_out);
endmodule
