// Digital circuit 3dot14function.dig as structural Verilog
module _3dot14function (
  input  a,
  input  b,
  input  c,
  output q
);

  wire not_1_out, not_2_out, not_3_out, or_1_out, or_2_out, or_3_out;

  not not_1 (not_1_out, a);
  not not_2 (not_2_out, c);
  not not_3 (not_3_out, b);
  or or_1 (or_1_out, a, not_3_out, c);
  or or_2 (or_2_out, not_1_out, b, not_2_out);
  or or_3 (or_3_out, not_1_out, not_3_out, not_2_out);
  nand nand_1 (q, or_1_out, or_2_out, or_3_out);
endmodule
