// Digital circuit 3dot9functionc.dig as structural Verilog
module _3dot9functionc (
  input  a,
  input  b,
  input  c,
  output q
);

  wire and_1_out, and_2_out, not_1_out, not_2_out, not_3_out;

  not not_1 (not_1_out, a);
  not not_2 (not_2_out, b);
  not not_3 (not_3_out, c);
  and and_1 (and_1_out, not_1_out, b);
  and and_2 (and_2_out, a, not_2_out);
  or or_1 (q, and_1_out, and_2_out, not_3_out);
endmodule
