// Digital circuit 3dot9functiond.dig as structural Verilog
module _3dot9functiond (
  input  a,
  input  b,
  input  c,
  output q
);

  wire not_1_out, xor_1_out;

  xor xor_1 (xor_1_out, b, a);
  not not_1 (not_1_out, c);
  or or_1 (q, xor_1_out, not_1_out);
endmodule
