// Digital circuit 3to8decoder.dig as structural Verilog
module _3to8decoder (
  input  E,
  input  I_2,
  input  I_1,
  input  I_0,
  output O_0,
  output O_1,
  output O_2,
  output O_3,
  output O_4,
  output O_5,
  output O_6,
  output O_7
);

  wire not_1_out, not_2_out, not_3_out;

  not not_1 (not_1_out, I_2);
  not not_2 (not_2_out, I_1);
  not not_3 (not_3_out, I_0);
  and and_1 (O_0, E, not_3_out, not_2_out, not_1_out);
  and and_2 (O_1, E, I_0, not_2_out, not_1_out);
  and and_3 (O_2, E, not_3_out, I_1, not_1_out);
  and and_4 (O_3, E, I_0, I_1, not_1_out);
  and and_5 (O_4, E, not_3_out, not_2_out, I_2);
  and and_6 (O_5, E, I_0, not_2_out, I_2);
  and and_7 (O_6, E, not_3_out, I_1, I_2);
  and and_8 (O_7, E, I_0, I_1, I_2);
endmodule
