// Digital circuit 4bitcarry_lookahead_adder.dig as structural Verilog
module _4bitcarry_lookahead_adder (
  input  A_3,
  input  B_3,
  input  A_2,
  input  B_2,
  input  A_1,
  input  B_1,
  input  A_0,
  input  B_0,
  input  C_in,
  output S_0,
  output S_1,
  output S_2,
  output S_3,
  output C_out
);

  wire and_1_out, and_2_out, and_3_out, and_4_out, and_5_out, and_6_out, and_7_out, and_8_out, or_1_out,
       or_2_out, or_3_out, or_4_out, or_5_out, or_6_out, or_7_out;

  and and_1 (and_1_out, A_3, B_3);
  or or_1 (or_1_out, A_3, B_3);
  and and_2 (and_2_out, A_2, B_2);
  or or_2 (or_2_out, A_2, B_2);
  and and_3 (and_3_out, A_1, B_1);
  or or_3 (or_3_out, A_1, B_1);
  and and_4 (and_4_out, A_0, B_0);
  or or_4 (or_4_out, A_0, B_0);
  xor xor_1 (S_0, and_4_out, or_4_out, C_in);
  and and_5 (and_5_out, or_4_out, C_in);
  or or_5 (or_5_out, and_4_out, and_5_out);
  xor xor_2 (S_1, or_5_out, and_3_out, or_3_out);
  and and_6 (and_6_out, or_3_out, or_5_out);
  or or_6 (or_6_out, and_3_out, and_6_out);
  xor xor_3 (S_2, or_6_out, and_2_out, or_2_out);
  and and_7 (and_7_out, or_2_out, or_6_out);
  or or_7 (or_7_out, and_2_out, and_7_out);
  xor xor_4 (S_3, or_7_out, and_1_out, or_1_out);
  and and_8 (and_8_out, or_1_out, or_7_out);
  or or_8 (C_out, and_1_out, and_8_out);
endmodule
