// Digital circuit 4bitcimparator.dig as structural Verilog
module _4bitcimparator (
  input  B2,
  input  A2,
  input  B1,
  input  A1,
  input  B0,
  input  A0,
  input  B3,
  input  A3,
  input  _1,
  input  _0,
  output A_eq_B,
  output A_lt_B,
  output A_gt_B
);

  wire enhanced1bitcomparator_1_a_eq_b_out, enhanced1bitcomparator_1_a_gt_b_out,
       enhanced1bitcomparator_1_a_lt_b_out, enhanced1bitcomparator_2_a_eq_b_out,
       enhanced1bitcomparator_2_a_gt_b_out, enhanced1bitcomparator_2_a_lt_b_out,
       enhanced1bitcomparator_3_a_eq_b_out, enhanced1bitcomparator_3_a_gt_b_out,
       enhanced1bitcomparator_3_a_lt_b_out;

  enhanced1bitcomparator enhanced1bitcomparator_1 (
    .A(A3), .B(B3), .A_gt_B_in(_0), .A_eq_B_in(_1), .A_lt_B_in(_0),
    .A_gt_B_out(enhanced1bitcomparator_1_a_gt_b_out), .A_eq_B_out(enhanced1bitcomparator_1_a_eq_b_out),
    .A_lt_B_out(enhanced1bitcomparator_1_a_lt_b_out));
  enhanced1bitcomparator enhanced1bitcomparator_2 (
    .A(A2), .B(B2), .A_gt_B_in(enhanced1bitcomparator_1_a_gt_b_out),
    .A_eq_B_in(enhanced1bitcomparator_1_a_eq_b_out), .A_lt_B_in(enhanced1bitcomparator_1_a_lt_b_out),
    .A_gt_B_out(enhanced1bitcomparator_2_a_gt_b_out), .A_eq_B_out(enhanced1bitcomparator_2_a_eq_b_out),
    .A_lt_B_out(enhanced1bitcomparator_2_a_lt_b_out));
  enhanced1bitcomparator enhanced1bitcomparator_3 (
    .A(A1), .B(B1), .A_gt_B_in(enhanced1bitcomparator_2_a_gt_b_out),
    .A_eq_B_in(enhanced1bitcomparator_2_a_eq_b_out), .A_lt_B_in(enhanced1bitcomparator_2_a_lt_b_out),
    .A_gt_B_out(enhanced1bitcomparator_3_a_gt_b_out), .A_eq_B_out(enhanced1bitcomparator_3_a_eq_b_out),
    .A_lt_B_out(enhanced1bitcomparator_3_a_lt_b_out));
  enhanced1bitcomparator enhanced1bitcomparator_4 (
    .A(A0), .B(B0), .A_gt_B_in(enhanced1bitcomparator_3_a_gt_b_out),
    .A_eq_B_in(enhanced1bitcomparator_3_a_eq_b_out), .A_lt_B_in(enhanced1bitcomparator_3_a_lt_b_out),
    .A_gt_B_out(A_gt_B), .A_eq_B_out(A_eq_B), .A_lt_B_out(A_lt_B));

  // Notes on the sheet:
  //   _1: default 1
endmodule
