// Digital circuit 4bitcomparator.dig as structural Verilog
module _4bitcomparator (
  input  B_2,
  input  A_2,
  input  B_1,
  input  A_1,
  input  B_0,
  input  A_0,
  input  B_3,
  input  A_3,
  output A_eq_B,
  output A_lt_B,
  output A_gt_B
);

  wire enhanced1bitcomparator_1_a_eq_b_out, enhanced1bitcomparator_1_a_gt_b_out,
       enhanced1bitcomparator_1_a_lt_b_out, enhanced1bitcomparator_2_a_eq_b_out,
       enhanced1bitcomparator_2_a_gt_b_out, enhanced1bitcomparator_2_a_lt_b_out,
       enhanced1bitcomparator_3_a_eq_b_out, enhanced1bitcomparator_3_a_gt_b_out,
       enhanced1bitcomparator_3_a_lt_b_out;

  enhanced1bitcomparator enhanced1bitcomparator_1 (
    .A(A_3), .B(B_3), .A_gt_B_in(1'b0), .A_eq_B_in(1'b1), .A_lt_B_in(1'b0),
    .A_gt_B_out(enhanced1bitcomparator_1_a_gt_b_out), .A_eq_B_out(enhanced1bitcomparator_1_a_eq_b_out),
    .A_lt_B_out(enhanced1bitcomparator_1_a_lt_b_out));
  enhanced1bitcomparator enhanced1bitcomparator_2 (
    .A(A_2), .B(B_2), .A_gt_B_in(enhanced1bitcomparator_1_a_gt_b_out),
    .A_eq_B_in(enhanced1bitcomparator_1_a_eq_b_out), .A_lt_B_in(enhanced1bitcomparator_1_a_lt_b_out),
    .A_gt_B_out(enhanced1bitcomparator_2_a_gt_b_out), .A_eq_B_out(enhanced1bitcomparator_2_a_eq_b_out),
    .A_lt_B_out(enhanced1bitcomparator_2_a_lt_b_out));
  enhanced1bitcomparator enhanced1bitcomparator_3 (
    .A(A_1), .B(B_1), .A_gt_B_in(enhanced1bitcomparator_2_a_gt_b_out),
    .A_eq_B_in(enhanced1bitcomparator_2_a_eq_b_out), .A_lt_B_in(enhanced1bitcomparator_2_a_lt_b_out),
    .A_gt_B_out(enhanced1bitcomparator_3_a_gt_b_out), .A_eq_B_out(enhanced1bitcomparator_3_a_eq_b_out),
    .A_lt_B_out(enhanced1bitcomparator_3_a_lt_b_out));
  enhanced1bitcomparator enhanced1bitcomparator_4 (
    .A(A_0), .B(B_0), .A_gt_B_in(enhanced1bitcomparator_3_a_gt_b_out),
    .A_eq_B_in(enhanced1bitcomparator_3_a_eq_b_out), .A_lt_B_in(enhanced1bitcomparator_3_a_lt_b_out),
    .A_gt_B_out(A_gt_B), .A_eq_B_out(A_eq_B), .A_lt_B_out(A_lt_B));
endmodule
