// Digital circuit 4to16from2to4decoder.dig as structural Verilog
module _4to16from2to4decoder (
  input  I_3,
  input  I_2,
  input  I_1,
  input  I_0,
  input  E,
  output O_0,
  output O_1,
  output O_2,
  output O_3,
  output O_4,
  output O_5,
  output O_6,
  output O_7,
  output O_8,
  output O_9,
  output O_10,
  output O_11,
  output O_12,
  output O_13,
  output O_14,
  output O_15
);

  wire _2to4decoder_1_o_0, _2to4decoder_1_o_1, _2to4decoder_1_o_2, _2to4decoder_1_o_3;

  _2to4decoder _2to4decoder_1 (
    .E(E), .I_0(I_2), .I_1(I_3), .O_0(_2to4decoder_1_o_0), .O_1(_2to4decoder_1_o_1),
    .O_2(_2to4decoder_1_o_2), .O_3(_2to4decoder_1_o_3));
  _2to4decoder _2to4decoder_2 (
    .E(_2to4decoder_1_o_0), .I_0(I_0), .I_1(I_1), .O_0(O_0), .O_1(O_1), .O_2(O_2), .O_3(O_3));
  _2to4decoder _2to4decoder_3 (
    .E(_2to4decoder_1_o_1), .I_0(I_0), .I_1(I_1), .O_0(O_4), .O_1(O_5), .O_2(O_6), .O_3(O_7));
  _2to4decoder _2to4decoder_4 (
    .E(_2to4decoder_1_o_2), .I_0(I_0), .I_1(I_1), .O_0(O_8), .O_1(O_9), .O_2(O_10), .O_3(O_11));
  _2to4decoder _2to4decoder_5 (
    .E(_2to4decoder_1_o_3), .I_0(I_0), .I_1(I_1), .O_0(O_12), .O_1(O_13), .O_2(O_14), .O_3(O_15));
endmodule
