// Digital circuit 4to16from3to8decoder.dig as structural Verilog
module _4to16from3to8decoder (
  input  I_3,
  input  I_2,
  input  I_1,
  input  I_0,
  output O_0,
  output O_1,
  output O_2,
  output O_3,
  output O_4,
  output O_5,
  output O_6,
  output O_7,
  output O_8,
  output O_9,
  output O_10,
  output O_11,
  output O_12,
  output O_13,
  output O_14,
  output O_15
);

  wire not_1_out;

  not not_1 (not_1_out, I_3);
  _3to8decoder _3to8decoder_1 (
    .E(not_1_out), .I2(I_2), .I1(I_1), .I0(I_0), .O0(O_0), .O1(O_1), .O2(O_2), .O3(O_3), .O4(O_4), .O5(O_5),
    .O6(O_6), .O7(O_7));
  _3to8decoder _3to8decoder_2 (
    .E(I_3), .I2(I_2), .I1(I_1), .I0(I_0), .O0(O_8), .O1(O_9), .O2(O_10), .O3(O_11), .O4(O_12), .O5(O_13),
    .O6(O_14), .O7(O_15));
endmodule
