// Digital circuit 5dot2function.dig as structural Verilog
module _5dot2function (
  input  c,
  input  b,
  input  a,
  input  _1,
  output q
);

  wire _3to8decoder_1_o2, _3to8decoder_1_o5, _3to8decoder_1_o7;

  _3to8decoder _3to8decoder_1 (
    .E(_1), .I2(a), .I1(b), .I0(c), .O2(_3to8decoder_1_o2), .O5(_3to8decoder_1_o5), .O7(_3to8decoder_1_o7));  // open: O0, O1, O3, O4, O6
  or or_1 (q, _3to8decoder_1_o2, _3to8decoder_1_o5, _3to8decoder_1_o7);

  // Notes on the sheet:
  //   _1: default 1
endmodule
