// Digital circuit 5dot6function.dig as structural Verilog
module _5dot6function (
  input  b,
  input  a,
  input  _0,
  input  c,
  input  _1,
  output q
);

  _4to1multiplexer _4to1multiplexer_1 (.S0(b), .S1(a), .E(_1), .I0(_0), .I1(_0), .I2(_0), .I3(c), .O0(q));

  // Notes on the sheet:
  //   _1: default 1
endmodule
