// Digital circuit 5dot7function.dig as structural Verilog
module _5dot7function (
  input  b,
  input  a,
  input  c,
  input  _1,
  output q
);

  wire not_1_out;

  not not_1 (not_1_out, c);
  _4to1multiplexer _4to1multiplexer_1 (.S0(b), .S1(a), .E(_1), .I0(c), .I1(not_1_out), .I2(c), .I3(not_1_out), .O0(q));

  // Notes on the sheet:
  //   _1: default 1
endmodule
