// Digital circuit 5dot8function.dig as structural Verilog
module _5dot8function (
  input  c,
  input  b,
  input  _0,
  input  _1,
  output q
);

  _4to1multiplexer _4to1multiplexer_1 (.S0(c), .S1(b), .E(_1), .I0(_0), .I1(_1), .I2(_1), .I3(_0), .O0(q));

  // Notes on the sheet:
  //   _1: default 1
endmodule
