// Digital circuit 8_to_3_encoder.dig as structural Verilog
module _8_to_3_encoder (
  input  I7,
  input  I6,
  input  I5,
  input  I4,
  input  I3,
  input  I2,
  input  I1,
  input  I0,
  output O2,
  output O1,
  output O0,
  output V
);

  or or_1 (O2, I4, I5, I6, I7);
  or or_2 (O1, I2, I3, I6, I7);
  or or_3 (O0, I1, I3, I5, I7);
  or or_4 (V, I0, I1, I2, I3, I4, I5, I6, I7);
endmodule
