// Digital circuit 8bit_register.dig as structural Verilog
module _8bit_register (
  input  Clk,
  input  D7,
  input  D6,
  input  D5,
  input  D4,
  input  D3,
  input  D2,
  input  D1,
  input  D0,
  output Q0,
  output Q1,
  output Q2,
  output Q3,
  output Q4,
  output Q5,
  output Q6,
  output Q7
);

  D_FF d_ff_1 (.D(D7), .C(Clk), .Q(Q7));  // open: nQ
  D_FF d_ff_2 (.D(D6), .C(Clk), .Q(Q6));  // open: nQ
  D_FF d_ff_3 (.D(D5), .C(Clk), .Q(Q5));  // open: nQ
  D_FF d_ff_4 (.D(D4), .C(Clk), .Q(Q4));  // open: nQ
  D_FF d_ff_5 (.D(D3), .C(Clk), .Q(Q3));  // open: nQ
  D_FF d_ff_6 (.D(D2), .C(Clk), .Q(Q2));  // open: nQ
  D_FF d_ff_7 (.D(D1), .C(Clk), .Q(Q1));  // open: nQ
  D_FF d_ff_8 (.D(D0), .C(Clk), .Q(Q0));  // open: nQ
endmodule
