// Digital circuit 8bit_shitleft_register.dig as structural Verilog
module _8bit_shitleft_register (
  input  Clk,
  input  _0,
  input  SHIFT,
  output Q7,
  output Q6,
  output Q5,
  output Q4,
  output Q3,
  output Q2,
  output Q1,
  output Q0
);

  wire and_1_out;

  and and_1 (and_1_out, Clk, SHIFT);
  D_FF d_ff_1 (.D(_0), .C(and_1_out), .Q(Q0));  // open: nQ
  D_FF d_ff_2 (.D(Q0), .C(and_1_out), .Q(Q1));  // open: nQ
  D_FF #(.Default(1)) d_ff_3 (.D(Q1), .C(and_1_out), .Q(Q2));  // open: nQ
  D_FF #(.Default(1)) d_ff_4 (.D(Q2), .C(and_1_out), .Q(Q3));  // open: nQ
  D_FF d_ff_5 (.D(Q3), .C(and_1_out), .Q(Q4));  // open: nQ
  D_FF d_ff_6 (.D(Q4), .C(and_1_out), .Q(Q5));  // open: nQ
  D_FF d_ff_7 (.D(Q5), .C(and_1_out), .Q(Q6));  // open: nQ
  D_FF d_ff_8 (.D(Q6), .C(and_1_out), .Q(Q7));  // open: nQ
endmodule
