// Digital circuit 8to1multiplexerfrom3to8decoder.dig as structural Verilog
module _8to1multiplexerfrom3to8decoder (
  input  I_0,
  input  I_1,
  input  I_2,
  input  I_3,
  input  I_4,
  input  I_5,
  input  I_6,
  input  I_7,
  input  E,
  input  S_2,
  input  S_1,
  input  S_0,
  output O
);

  wire _3to8decoder_1_o0, _3to8decoder_1_o1, _3to8decoder_1_o2, _3to8decoder_1_o3, _3to8decoder_1_o4,
       _3to8decoder_1_o5, _3to8decoder_1_o6, _3to8decoder_1_o7, and_1_out, and_2_out, and_3_out, and_4_out,
       and_5_out, and_6_out, and_7_out, and_8_out, or_1_out, or_2_out;

  _3to8decoder _3to8decoder_1 (
    .E(E), .I2(S_2), .I1(S_1), .I0(S_0), .O0(_3to8decoder_1_o0), .O1(_3to8decoder_1_o1),
    .O2(_3to8decoder_1_o2), .O3(_3to8decoder_1_o3), .O4(_3to8decoder_1_o4), .O5(_3to8decoder_1_o5),
    .O6(_3to8decoder_1_o6), .O7(_3to8decoder_1_o7));
  and and_1 (and_1_out, _3to8decoder_1_o0, I_0);
  and and_2 (and_2_out, _3to8decoder_1_o1, I_1);
  and and_3 (and_3_out, _3to8decoder_1_o2, I_2);
  and and_4 (and_4_out, _3to8decoder_1_o3, I_3);
  and and_5 (and_5_out, _3to8decoder_1_o4, I_4);
  and and_6 (and_6_out, _3to8decoder_1_o5, I_5);
  and and_7 (and_7_out, _3to8decoder_1_o6, I_6);
  and and_8 (and_8_out, _3to8decoder_1_o7, I_7);
  or or_1 (or_1_out, and_1_out, and_2_out, and_3_out, and_4_out);
  or or_2 (or_2_out, and_5_out, and_6_out, and_7_out, and_8_out);
  or or_3 (O, or_1_out, or_2_out);
endmodule
