// Digital circuit 8to3encoder.dig as structural Verilog
module _8to3encoder (
  input  I_0,
  input  I_2,
  input  I_3,
  input  I_4,
  input  I_5,
  input  I_6,
  input  I_7,
  input  I_1,
  output O_2,
  output O_1,
  output O_0,
  output V
);

  or or_1 (O_2, I_4, I_5, I_6, I_7);
  or or_2 (O_1, I_2, I_3, I_6, I_7);
  or or_3 (O_0, I_1, I_3, I_5, I_7);
  or or_4 (V, I_0, I_1, I_2, I_3, I_4, I_5, I_6, I_7);
endmodule
