// Digital circuit bcd7decoder.dig as structural Verilog
module bcd7decoder (
  input  I_3,
  input  I_2,
  input  I_1,
  input  I_0,
  output a,
  output b,
  output c,
  output d,
  output e,
  output f,
  output g
);

  wire and_1_out, and_2_out, and_3_out, and_4_out, and_5_out, and_6_out, and_7_out, and_8_out, and_9_out,
       and_10_out, and_11_out, and_12_out, and_13_out, and_14_out, and_15_out, and_16_out, and_17_out,
       not_1_out, not_2_out, not_3_out;

  not not_1 (not_1_out, I_2);
  not not_2 (not_2_out, I_1);
  not not_3 (not_3_out, I_0);
  and and_1 (and_1_out, not_3_out, not_1_out);
  and and_2 (and_2_out, I_0, I_2);
  and and_3 (and_3_out, not_3_out, not_2_out);
  and and_4 (and_4_out, I_0, I_1);
  or or_1 (c, I_0, not_2_out, I_2);
  and and_5 (and_5_out, not_3_out, not_1_out);
  and and_6 (and_6_out, I_0, not_2_out, I_2);
  and and_7 (and_7_out, not_3_out, I_1);
  and and_8 (and_8_out, I_1, not_1_out);
  and and_9 (and_9_out, not_3_out, not_1_out);
  and and_10 (and_10_out, not_3_out, I_1);
  and and_11 (and_11_out, not_3_out, not_2_out);
  and and_12 (and_12_out, not_3_out, I_2);
  and and_13 (and_13_out, not_2_out, I_2);
  and and_14 (and_14_out, not_2_out, I_3);
  and and_15 (and_15_out, not_3_out, I_1);
  and and_16 (and_16_out, I_1, not_1_out);
  and and_17 (and_17_out, not_2_out, I_2);
  or or_2 (b, and_3_out, and_4_out, not_1_out);
  or or_3 (e, and_9_out, and_10_out);
  or or_4 (a, and_1_out, and_2_out, I_1, I_3);
  or or_5 (d, and_5_out, and_6_out, and_7_out, and_8_out, I_3);
  or or_6 (f, and_11_out, and_12_out, and_13_out, and_14_out);
  or or_7 (g, and_15_out, and_16_out, and_17_out, I_3);
endmodule
