// Digital circuit d_flip.dig as structural Verilog
module d_flip (
  input  D,
  input  CLK,
  output Q,
  output Q_2
);

  wire d_latch_1_q, not_1_out;

  not not_1 (not_1_out, CLK);
  d_latch d_latch_1 (.D(D), .E(not_1_out), .Q(d_latch_1_q));  // open: Q_2
  d_latch d_latch_2 (.D(d_latch_1_q), .E(CLK), .Q(Q), .Q_2(Q_2));
endmodule
