// Digital circuit d_flip_present_0.dig as structural Verilog
module d_flip_present_0 (
  input  CLK,
  input  D,
  output Q,
  output Q0
);

  wire nand_1_out, nand_2_out, nand_3_out, nand_4_out;

  nand nand_1 (nand_1_out, nand_4_out, nand_2_out);
  nand nand_2 (nand_2_out, nand_1_out, CLK);
  nand nand_3 (nand_3_out, nand_2_out, CLK, nand_4_out);
  nand nand_4 (nand_4_out, nand_3_out, D);
  nand nand_5 (Q, nand_2_out, Q0);
  nand nand_6 (Q0, Q, nand_3_out);
endmodule
