// Digital circuit enhanced1bitcomparator.dig as structural Verilog
module enhanced1bitcomparator (
  input  A,
  input  B,
  input  A_gt_B_in,
  input  A_eq_B_in,
  input  A_lt_B_in,
  output A_gt_B_out,
  output A_eq_B_out,
  output A_lt_B_out
);

  wire and_1_out, and_2_out, not_1_out, not_2_out;

  not not_1 (not_1_out, A);
  not not_2 (not_2_out, B);
  and and_1 (and_1_out, A_eq_B_in, A, not_2_out);
  and and_2 (and_2_out, not_1_out, B, A_eq_B_in);
  or or_1 (A_gt_B_out, A_gt_B_in, and_1_out);
  or or_2 (A_lt_B_out, and_2_out, A_lt_B_in);
  nor nor_1 (A_eq_B_out, A_gt_B_out, A_lt_B_out);
endmodule
