// Digital circuit generic8to1multiplexer.dig as structural Verilog
module generic8to1multiplexer (
  input  I_0,
  input  I_1,
  input  I_2,
  input  I_3,
  input  I_4,
  input  I_5,
  input  I_6,
  input  I_7,
  input  [2:0] S,
  output O_0
);

  Multiplexer #(.Selector_Bits(3)) multiplexer_1 (
    .sel(S), .in_0(I_0), .in_1(I_1), .in_2(I_2), .in_3(I_3), .in_4(I_4), .in_5(I_5), .in_6(I_6), .in_7(I_7),
    .out(O_0));
endmodule
