// Digital circuit halfadder.dig as structural Verilog
module halfadder (
  input  A,
  input  B,
  output C,
  output S
);

  wire and_2_out, and_3_out, not_1_out, not_2_out;

  not not_1 (not_1_out, A);
  not not_2 (not_2_out, B);
  and and_1 (C, A, B);
  and and_2 (and_2_out, not_1_out, B);
  and and_3 (and_3_out, A, not_2_out);
  or or_1 (S, and_2_out, and_3_out);
endmodule
