// Digital circuit jk_flipflop_d.dig as structural Verilog
module jk_flipflop_d (
  input  CLK,
  input  J,
  input  K,
  output Q,
  output Q_2
);

  wire and_1_out, and_2_out, not_1_out, or_1_out;

  not not_1 (not_1_out, K);
  and and_1 (and_1_out, Q, J);
  and and_2 (and_2_out, not_1_out, Q_2);
  or or_1 (or_1_out, and_1_out, and_2_out);
  d_flip d_flip_1 (.D(or_1_out), .CLK(CLK), .Q(Q_2), .Q_2(Q));
endmodule
