// Digital circuit jk_flipflop_sr.dig as structural Verilog
module jk_flipflop_sr (
  input  J,
  input  CLK,
  input  K,
  output Q,
  output Q_2
);

  wire and_1_out, and_2_out, and_3_out, and_4_out, not_1_out, s_r_latch_nand_1_q, s_r_latch_nand_1_q_2;

  not not_1 (not_1_out, CLK);
  and and_1 (and_1_out, Q_2, not_1_out, J);
  and and_2 (and_2_out, K, not_1_out, Q);
  s_r_latch_nand s_r_latch_nand_1 (.S(and_1_out), .R(and_2_out), .Q(s_r_latch_nand_1_q), .Q_2(s_r_latch_nand_1_q_2));
  and and_3 (and_3_out, s_r_latch_nand_1_q, CLK);
  and and_4 (and_4_out, s_r_latch_nand_1_q_2, CLK);
  s_r_latch_nand s_r_latch_nand_2 (.S(and_3_out), .R(and_4_out), .Q(Q), .Q_2(Q_2));
endmodule
