// Digital circuit lookup_rom_2output.dig as structural Verilog
module lookup_rom_2output (
  input  b,
  input  c,
  input  a,
  output [1:0] q
);

  LookUpTable #(.Bits(2)) lookuptable_1 (.in0(c), .in1(b), .in2(a), .out(q));

  // Notes on the sheet:
  //   contents of lookuptable_1 (hex, n*v repeats v):
  //   0,6*1,3
endmodule
