// Digital circuit lookup_rom_arch.dig as structural Verilog
module lookup_rom_arch (
  input  Y1,
  input  Y0,
  input  X0,
  input  X1,
  output [3:0] q
);

  LookUpTable #(.Bits(4)) lookuptable_1 (.in0(Y0), .in1(Y1), .in2(X0), .in3(X1), .out(q));

  // Notes on the sheet:
  //   contents of lookuptable_1 (hex, n*v repeats v):
  //   5*0,1,2,3,0,2,4,6,0,3,6,9
endmodule
