// Digital circuit nand_3input_cmos.dig as structural Verilog
module nand_3input_cmos (
  input  A,
  input  B,
  input  C,
  output Out
);

  wire M1_s, M2_s;

  PFET #(.unidirectional("true")) M4 (.G(A), .S(1'b1), .D(Out));
  PFET #(.unidirectional("true")) M5 (.G(B), .S(1'b1), .D(Out));
  NFET #(.unidirectional("true")) M1 (.G(A), .D(Out), .S(M1_s));
  NFET #(.unidirectional("true")) M2 (.G(B), .D(M1_s), .S(M2_s));
  NFET #(.unidirectional("true")) M3 (.G(C), .D(M2_s), .S(1'b0));
  PFET #(.unidirectional("true")) M6 (.G(C), .S(1'b1), .D(Out));
endmodule
