// Digital circuit nand_cmos.dig as structural Verilog
module nand_cmos (
  input  A,
  input  B,
  output Out
);

  wire M1_s;

  PFET #(.unidirectional("true")) M3 (.G(A), .S(1'b1), .D(Out));
  NFET #(.unidirectional("true")) M1 (.G(A), .D(Out), .S(M1_s));
  NFET #(.unidirectional("true")) M2 (.G(B), .D(M1_s), .S(1'b0));
  PFET #(.unidirectional("true")) M4 (.G(B), .S(1'b1), .D(Out));
endmodule
