// Digital circuit nor_3input_cmos.dig as structural Verilog
module nor_3input_cmos (
  input  A,
  input  B,
  input  C,
  output Out
);

  wire M4_d, M5_d;

  NFET #(.unidirectional("true")) M1 (.G(A), .D(Out), .S(1'b0));
  PFET #(.unidirectional("true")) M4 (.G(A), .S(1'b1), .D(M4_d));
  PFET #(.unidirectional("true")) M5 (.G(B), .S(M4_d), .D(M5_d));
  PFET #(.unidirectional("true")) M6 (.G(C), .S(M5_d), .D(Out));
  NFET #(.unidirectional("true")) M2 (.G(B), .D(Out), .S(1'b0));
  NFET #(.unidirectional("true")) M3 (.G(C), .D(Out), .S(1'b0));
endmodule
