// Digital circuit nor_cmos.dig as structural Verilog
module nor_cmos (
  input  A,
  input  B,
  output Out
);

  wire pfet_1_d;

  NFET nfet_1 (.G(A), .D(Out), .S(1'b0));
  PFET pfet_1 (.G(A), .S(1'b1), .D(pfet_1_d));
  PFET pfet_2 (.G(B), .S(pfet_1_d), .D(Out));
  NFET nfet_2 (.G(B), .D(Out), .S(1'b0));
endmodule
