// Digital circuit not_cmos.dig as structural Verilog
module not_cmos (
  input  In,
  output Out
);

  PFET #(.unidirectional("true")) M2 (.G(In), .S(1'b1), .D(Out));
  NFET #(.unidirectional("true")) M1 (.G(In), .D(Out), .S(1'b0));
endmodule
