// Digital circuit s_r_latch_nand.dig as structural Verilog
module s_r_latch_nand (
  input  S,
  input  R,
  output Q,
  output Q_2
);

  wire not_1_out, not_2_out;

  not not_1 (not_1_out, S);
  not not_2 (not_2_out, R);
  nand nand_1 (Q, not_1_out, Q_2);
  nand nand_2 (Q_2, Q, not_2_out);
endmodule
