// Digital circuit sram.dig as structural Verilog
module sram (
  input  in_1,
  output out_2,
  output out_3
);

  wire nfet_1_d, not_1_out;

  NFET nfet_1 (.G(in_1), .D(nfet_1_d), .S(out_3));
  not not_1 (not_1_out, nfet_1_d);
  not not_2 (nfet_1_d, not_1_out);
  NFET nfet_2 (.G(in_1), .D(out_2), .S(not_1_out));
endmodule
