// Digital circuit t_flipflop_jk.dig as structural Verilog
module t_flipflop_jk (
  input  T,
  input  CLK,
  output Q,
  output Q_2
);

  jk_flipflop_sr jk_flipflop_sr_1 (.J(T), .CLK(CLK), .K(T), .Q(Q), .Q_2(Q_2));
endmodule
