// Digital circuit 2_to_4_decoder.dig as structural Verilog
module _2_to_4_decoder (
  input  E,
  input  I1,
  input  I0,
  output O0,
  output O1,
  output O2,
  output O3
);

  wire not_1_out, not_2_out;

  not not_1 (not_1_out, I1);
  not not_2 (not_2_out, I0);
  and and_1 (O0, E, not_2_out, not_1_out);
  and and_2 (O1, E, I0, not_1_out);
  and and_3 (O2, E, not_2_out, I1);
  and and_4 (O3, E, I0, I1);
endmodule
