// Digital circuit 2to4decoder.dig as structural Verilog
module _2to4decoder (
  input  E,
  input  I0,
  input  I1,
  output O0,
  output O1,
  output O2,
  output O3
);

  wire not_1_out, not_2_out;

  not not_1 (not_1_out, I0);
  not not_2 (not_2_out, I1);
  and and_1 (O0, E, not_1_out, not_2_out);
  and and_2 (O1, E, I0, not_2_out);
  and and_3 (O2, E, not_1_out, I1);
  and and_4 (O3, E, I0, I1);
endmodule
