// Digital circuit 4to16from3to8decoder.dig as structural Verilog
module _4to16from3to8decoder (
  input  I3,
  input  I2,
  input  I1,
  input  I0,
  output O0,
  output O1,
  output O2,
  output O3,
  output O4,
  output O5,
  output O6,
  output O7,
  output O8,
  output O9,
  output O10,
  output O11,
  output O12,
  output O13,
  output O14,
  output O15
);

  wire not_1_out;

  not not_1 (not_1_out, I3);
  _3to8decoder _3to8decoder_1 (
    .E(not_1_out), .I_2(I2), .I_1(I1), .I_0(I0), .O_0(O0), .O_1(O1), .O_2(O2), .O_3(O3), .O_4(O4), .O_5(O5),
    .O_6(O6), .O_7(O7));
  _3to8decoder _3to8decoder_2 (
    .E(I3), .I_2(I2), .I_1(I1), .I_0(I0), .O_0(O8), .O_1(O9), .O_2(O10), .O_3(O11), .O_4(O12), .O_5(O13),
    .O_6(O14), .O_7(O15));
endmodule
