// Digital circuit 4to1multiplexer.dig as structural Verilog
module _4to1multiplexer (
  input  S0,
  input  S1,
  input  E,
  input  I0,
  input  I1,
  input  I2,
  input  I3,
  output O0
);

  wire and_1_out, and_2_out, and_3_out, and_4_out, not_1_out, not_2_out;

  not not_1 (not_1_out, S1);
  not not_2 (not_2_out, S0);
  and and_1 (and_1_out, not_2_out, not_1_out, I0, E);
  and and_2 (and_2_out, S0, not_1_out, I1, E);
  and and_3 (and_3_out, not_2_out, S1, I2, E);
  and and_4 (and_4_out, S0, S1, I3, E);
  or or_1 (O0, and_1_out, and_2_out, and_3_out, and_4_out);
endmodule
