// Digital circuit 5dot3functionb.dig as structural Verilog
module _5dot3functionb (
  input  c,
  input  b,
  input  a,
  input  _1,
  output q
);

  wire _3to8decoder_1_o0, _3to8decoder_1_o2, _3to8decoder_1_o3, _3to8decoder_1_o4, _3to8decoder_1_o5,
       _3to8decoder_1_o6, or_1_out, or_2_out;

  _3to8decoder _3to8decoder_1 (
    .E(_1), .I2(a), .I1(b), .I0(c), .O0(_3to8decoder_1_o0), .O2(_3to8decoder_1_o2), .O3(_3to8decoder_1_o3),
    .O4(_3to8decoder_1_o4), .O5(_3to8decoder_1_o5), .O6(_3to8decoder_1_o6));  // open: O1, O7
  or or_1 (or_1_out, _3to8decoder_1_o0, _3to8decoder_1_o2, _3to8decoder_1_o3);
  or or_2 (or_2_out, _3to8decoder_1_o4, _3to8decoder_1_o5, _3to8decoder_1_o6);
  or or_3 (q, or_1_out, or_2_out);

  // Notes on the sheet:
  //   _1: default 1
endmodule
