// Digital circuit 5dot3functionc.dig as structural Verilog
module _5dot3functionc (
  input  c,
  input  b,
  input  a,
  input  _1,
  output q
);

  wire _3to8decoder_1_o1, _3to8decoder_1_o7;

  _3to8decoder _3to8decoder_1 (
    .E(_1), .I2(a), .I1(b), .I0(c), .O1(_3to8decoder_1_o1), .O7(_3to8decoder_1_o7));  // open: O0, O2, O3, O4, O5, O6
  nor nor_1 (q, _3to8decoder_1_o1, _3to8decoder_1_o7);

  // Notes on the sheet:
  //   _1: default 1
endmodule
