// Digital circuit 5dot4function.dig as structural Verilog
module _5dot4function (
  input  S0,
  input  S1,
  input  S2,
  input  _1,
  input  _0,
  output q
);

  _8to1multiplexer _8to1multiplexer_1 (
    .S0(S0), .S1(S1), .S2(S2), .E(_1), .I0(_0), .I1(_0), .I2(_0), .I3(_0), .I4(_0), .I5(_0), .I6(_0),
    .I7(_1), .O0(q));

  // Notes on the sheet:
  //   _1: default 1
endmodule
