// Digital circuit 8bit_shiftright_register_jk.dig as structural Verilog
module _8bit_shiftright_register_jk (
  input  Clk,
  input  _0,
  input  SHIFT,
  output Q0,
  output Q1,
  output Q2,
  output Q3,
  output Q4,
  output Q5,
  output Q6,
  output Q7
);

  wire and_1_out, jk_ff_1_nq, jk_ff_2_nq, jk_ff_3_nq, jk_ff_4_nq, jk_ff_5_nq, jk_ff_6_nq, jk_ff_7_nq,
       not_1_out;

  and and_1 (and_1_out, Clk, SHIFT);
  not not_1 (not_1_out, _0);
  JK_FF jk_ff_1 (.J(_0), .C(and_1_out), .K(not_1_out), .Q(Q7), .nQ(jk_ff_1_nq));
  JK_FF jk_ff_2 (.J(Q7), .C(and_1_out), .K(jk_ff_1_nq), .Q(Q6), .nQ(jk_ff_2_nq));
  JK_FF #(.Default(1)) jk_ff_3 (.J(Q6), .C(and_1_out), .K(jk_ff_2_nq), .Q(Q5), .nQ(jk_ff_3_nq));
  JK_FF jk_ff_4 (.J(Q5), .C(and_1_out), .K(jk_ff_3_nq), .Q(Q4), .nQ(jk_ff_4_nq));
  JK_FF #(.Default(1)) jk_ff_5 (.J(Q4), .C(and_1_out), .K(jk_ff_4_nq), .Q(Q3), .nQ(jk_ff_5_nq));
  JK_FF jk_ff_6 (.J(Q3), .C(and_1_out), .K(jk_ff_5_nq), .Q(Q2), .nQ(jk_ff_6_nq));
  JK_FF jk_ff_7 (.J(Q2), .C(and_1_out), .K(jk_ff_6_nq), .Q(Q1), .nQ(jk_ff_7_nq));
  JK_FF jk_ff_8 (.J(Q1), .C(and_1_out), .K(jk_ff_7_nq), .Q(Q0));  // open: nQ
endmodule
