// Digital circuit 8to1multiplexerfrom3to8decoder.dig as structural Verilog
module _8to1multiplexerfrom3to8decoder (
  input  I0,
  input  I1,
  input  I2,
  input  I3,
  input  I4,
  input  I5,
  input  I6,
  input  I7,
  input  E,
  input  S2,
  input  S1,
  input  S0,
  output O0
);

  wire _3to8decoder_1_o_0, _3to8decoder_1_o_1, _3to8decoder_1_o_2, _3to8decoder_1_o_3, _3to8decoder_1_o_4,
       _3to8decoder_1_o_5, _3to8decoder_1_o_6, _3to8decoder_1_o_7, and_1_out, and_2_out, and_3_out,
       and_4_out, and_5_out, and_6_out, and_7_out, and_8_out, or_1_out, or_2_out;

  _3to8decoder _3to8decoder_1 (
    .E(E), .I_2(S2), .I_1(S1), .I_0(S0), .O_0(_3to8decoder_1_o_0), .O_1(_3to8decoder_1_o_1),
    .O_2(_3to8decoder_1_o_2), .O_3(_3to8decoder_1_o_3), .O_4(_3to8decoder_1_o_4), .O_5(_3to8decoder_1_o_5),
    .O_6(_3to8decoder_1_o_6), .O_7(_3to8decoder_1_o_7));
  and and_1 (and_1_out, _3to8decoder_1_o_0, I0);
  and and_2 (and_2_out, _3to8decoder_1_o_1, I1);
  and and_3 (and_3_out, _3to8decoder_1_o_2, I2);
  and and_4 (and_4_out, _3to8decoder_1_o_3, I3);
  and and_5 (and_5_out, _3to8decoder_1_o_4, I4);
  and and_6 (and_6_out, _3to8decoder_1_o_5, I5);
  and and_7 (and_7_out, _3to8decoder_1_o_6, I6);
  and and_8 (and_8_out, _3to8decoder_1_o_7, I7);
  or or_1 (or_1_out, and_1_out, and_2_out, and_3_out, and_4_out);
  or or_2 (or_2_out, and_5_out, and_6_out, and_7_out, and_8_out);
  or or_3 (O0, or_1_out, or_2_out);
endmodule
