// Digital circuit 8to3encoder.dig as structural Verilog
module _8to3encoder (
  input  I0,
  input  I1,
  input  I2,
  input  I3,
  input  I4,
  input  I5,
  input  I6,
  input  I7,
  output O2,
  output O1,
  output O0,
  output V
);

  or or_1 (O2, I4, I5, I6, I7);
  or or_2 (O1, I2, I3, I6, I7);
  or or_3 (O0, I1, I3, I5, I7);
  or or_4 (V, O2, O1, O0, I0);
endmodule
