// Digital circuit 8to3priorityencoder.dig as structural Verilog
module _8to3priorityencoder (
  input  I0,
  input  I1,
  input  I2,
  input  I3,
  input  I4,
  input  I5,
  input  I6,
  input  I7,
  output O2,
  output O1,
  output O0,
  output V
);

  wire and_1_out, and_2_out, and_3_out, and_4_out, nor_1_out, not_1_out, not_2_out, not_3_out, or_1_out;

  nor nor_1 (nor_1_out, I4, I5);
  not not_1 (not_1_out, I2);
  not not_2 (not_2_out, I4);
  not not_3 (not_3_out, I6);
  or or_1 (or_1_out, I2, I3);
  and and_1 (and_1_out, or_1_out, nor_1_out);
  and and_2 (and_2_out, not_1_out, not_2_out, I1, not_3_out);
  and and_3 (and_3_out, not_2_out, I3, not_3_out);
  and and_4 (and_4_out, not_3_out, I5);
  or or_2 (O2, I4, I5, I6, I7);
  or or_3 (O1, and_1_out, I6, I7);
  or or_4 (O0, and_2_out, and_3_out, and_4_out, I7);
  or or_5 (V, O2, O1, O0, I0);
endmodule
