// Digital circuit bcd7decoderLED.dig as structural Verilog
module bcd7decoderLED (
  input  I3,
  input  I2,
  input  I1,
  input  I0,
  input  _0
);

  wire bcd7decoder_1_a, bcd7decoder_1_b, bcd7decoder_1_c, bcd7decoder_1_d, bcd7decoder_1_e, bcd7decoder_1_f,
       bcd7decoder_1_g;

  bcd7decoder bcd7decoder_1 (
    .I3(I3), .I2(I2), .I1(I1), .I0(I0), .a(bcd7decoder_1_a), .b(bcd7decoder_1_b), .c(bcd7decoder_1_c),
    .d(bcd7decoder_1_d), .e(bcd7decoder_1_e), .f(bcd7decoder_1_f), .g(bcd7decoder_1_g));
  Seven_Seg seven_seg_1 (
    .a(bcd7decoder_1_a), .b(bcd7decoder_1_b), .c(bcd7decoder_1_c), .d(bcd7decoder_1_d), .e(bcd7decoder_1_e),
    .f(bcd7decoder_1_f), .g(bcd7decoder_1_g), .dp(_0));
endmodule
