// Digital circuit d_flip_present.dig as structural Verilog
module d_flip_present (
  input  CLK,
  input  PRE0,
  input  CLR0,
  input  D,
  output Q,
  output Q0
);

  wire nand_1_out, nand_2_out, nand_3_out, nand_4_out;

  nand nand_1 (nand_1_out, PRE0, nand_4_out, nand_2_out);
  nand nand_2 (nand_2_out, nand_1_out, CLR0, CLK);
  nand nand_3 (nand_3_out, nand_2_out, CLK, nand_4_out);
  nand nand_4 (nand_4_out, nand_3_out, CLR0, D);
  nand nand_5 (Q, PRE0, nand_2_out, Q0);
  nand nand_6 (Q0, Q, CLR0, nand_3_out);
endmodule
