// Digital circuit d_latch.dig as structural Verilog
module d_latch (
  input  D,
  input  E,
  output Q,
  output Q_2
);

  wire and_1_out, and_2_out, not_1_out;

  not not_1 (not_1_out, D);
  and and_1 (and_1_out, D, E);
  and and_2 (and_2_out, E, not_1_out);
  s_r_latch_nand s_r_latch_nand_1 (.S(and_1_out), .R(and_2_out), .Q(Q), .Q0(Q_2));
endmodule
