// Digital circuit decoder_p.dig as structural Verilog
module decoder_p (
  input  I1,
  input  [2:0] E,
  input  I3,
  input  I2,
  output O1,
  output O2,
  output O3,
  output O4,
  output O5,
  output O6,
  output O7,
  output O8
);

  Decoder #(.Selector_Bits(3)) decoder_1 (
    .sel(E), .out_0(O1), .out_1(O2), .out_2(O3), .out_3(O4), .out_4(O5), .out_5(O6), .out_6(O7), .out_7(O8));
  // Pins of 1 and 3 bits meet at E
endmodule
