// Digital circuit enhanced1bitcomparator.dig as structural Verilog
module enhanced1bitcomparator (
  input  A,
  input  B,
  input  A_gt_Bin,
  input  A_eq_Bin,
  input  A_lt_Bin,
  output A_gt_Bout,
  output A_eq_Bout,
  output A_lt_Bout
);

  wire and_1_out, and_2_out, not_1_out, not_2_out;

  not not_1 (not_1_out, A);
  not not_2 (not_2_out, B);
  and and_1 (and_1_out, A_eq_Bin, A, not_2_out);
  and and_2 (and_2_out, not_1_out, B, A_eq_Bin);
  or or_1 (A_gt_Bout, A_gt_Bin, and_1_out);
  or or_2 (A_lt_Bout, and_2_out, A_lt_Bin);
  nor nor_1 (A_eq_Bout, A_gt_Bout, A_lt_Bout);
endmodule
