// Digital circuit halfadder_nor.dig as structural Verilog
module halfadder_nor (
  input  A,
  input  B,
  output C,
  output S
);

  wire nor_1_out;

  nor nor_1 (nor_1_out, A, B);
  and and_1 (C, A, B);
  nor nor_2 (S, C, nor_1_out);
endmodule
