// Digital circuit jk_flip_flop_preset.dig as structural Verilog
module jk_flip_flop_preset (
  input  J,
  input  K,
  input  PRE,
  input  CLR,
  input  CLK,
  output Q,
  output Q_2
);

  wire and_1_out, and_2_out, and_3_out, and_4_out, nand_1_out, nand_2_out, not_1_out;

  not not_1 (not_1_out, CLK);
  nand nand_1 (nand_1_out, CLR, J, not_1_out);
  nand nand_2 (nand_2_out, not_1_out, K, PRE);
  and and_1 (and_1_out, Q_2, nand_1_out, PRE);
  and and_2 (and_2_out, Q_2, not_1_out, PRE);
  and and_3 (and_3_out, CLR, not_1_out, Q);
  and and_4 (and_4_out, CLR, nand_2_out, Q);
  nor nor_1 (Q, and_1_out, and_2_out);
  nor nor_2 (Q_2, and_3_out, and_4_out);
endmodule
