// Digital circuit lookup_rom_and.dig as structural Verilog
module lookup_rom_and (
  input  b,
  input  c,
  input  a,
  output q
);

  LookUpTable lookuptable_1 (.in0(c), .in1(b), .in2(a), .out(q));

  // Notes on the sheet:
  //   contents of lookuptable_1 (hex, n*v repeats v):
  //   7*0,1
endmodule
