// Digital circuit rippleadder.dig as structural Verilog
module rippleadder (
  input  _0,
  input  A0,
  input  B0,
  input  A0_2,
  input  B1,
  output S0,
  output S1,
  output Cout
);

  wire fulladder_2_c_out;

  fulladder fulladder_1 (.A(A0_2), .B(B1), .C_in(fulladder_2_c_out), .C_out(Cout), .S(S1));
  fulladder fulladder_2 (.A(A0), .B(B0), .C_in(_0), .C_out(fulladder_2_c_out), .S(S0));
endmodule
