// Digital circuit s_r_latch_enable.dig as structural Verilog
module s_r_latch_enable (
  input  S,
  input  R,
  input  E,
  output Q,
  output Q_2
);

  wire and_1_out, and_2_out;

  and and_1 (and_1_out, S, E);
  and and_2 (and_2_out, E, R);
  s_r_latch_nand s_r_latch_nand_1 (.S(and_1_out), .R(and_2_out), .Q(Q), .Q0(Q_2));
endmodule
