// Digital circuit t_flipflop_d.dig as structural Verilog
module t_flipflop_d (
  input  T,
  input  CLK,
  output Q,
  output Q_2
);

  wire xor_1_out;

  xor xor_1 (xor_1_out, Q, T);
  d_flip d_flip_1 (.D(xor_1_out), .CLK(CLK), .Q(Q), .Q0(Q_2));
endmodule
